# Fritzing sketch Cableado(Fritzing) (saved by Fritzing 0.9.3b)
circuit board: 8.46667cm x 5.64444cm
breadboards: 2

parts:
  LCD1 = LCD screen
  R1 = Resistor [tolerance=±5% resistance=10k package="2010 [SMD]"]
  Componente1 = Arduino Uno (Rev3)
  R2 = Trimmer Potentiometer [maximum_resistance=10kΩ package=THT]  # not connected
  U1 = 7-SEGMENT-DISPLAY [package=7-segment-display]
  S1 = Pushbutton [package="[SMD]"]
  S2 = Pushbutton [package="[SMD]"]
  S3 = Pushbutton [package="[SMD]"]
  U2 = 74HC595 [package="DIP16 [THT]"]
  R3 = Resistor [tolerance=±5% resistance=10k package="2010 [SMD]"]
  R4 = Resistor [tolerance=±5% resistance=10k package="2010 [SMD]"]
  R5 = Resistor [tolerance=±5% resistance=10k package="2010 [SMD]"]
  R6 = Resistor [tolerance=±5% resistance=220 package=THT]
  R7 = Resistor [tolerance=±5% resistance=220 package=THT]
  R8 = Resistor [tolerance=±5% resistance=220 package=THT]
  R9 = Resistor [tolerance=±5% resistance=220 package=THT]
  R10 = Resistor [tolerance=±5% resistance=220 package=THT]
  R11 = Resistor [tolerance=±5% resistance=220 package=THT]
  R12 = Resistor [tolerance=±5% resistance=220 package=THT]

nets:
  VSS: LCD1.VSS, LCD1.R/W, LCD1.LED-, Componente1.GND, U1.F, S1.Pin_3, S1.Pin_4, S2.Pin_3, S2.Pin_4, S3.Pin_3, S3.Pin_4
  VDD: LCD1.VDD, R1.Pin_0, Componente1.5V, U2.OE, U2.VCC, R3.Pin_0, R4.Pin_0, R5.Pin_0
  N1: LCD1.RS, Componente1.D11_PWM/MOSI
  N2: LCD1.E, Componente1.D12/MISO
  N3: LCD1.DB4, Componente1.D4
  N4: LCD1.DB5, Componente1.D5_PWM
  N5: LCD1.DB6, Componente1.D6_PWM
  N6: LCD1.DB7, Componente1.D7
  N7: LCD1.LED+, R1.Pin_1
  N8: Componente1.D8, U2.ST_CP
  N9: Componente1.D9_PWM, U2.DS
  N10: Componente1.D10_PWM/SS, U2.SH_CP
  N11: Componente1.D1/TX, S3.Pin_1, S3.Pin_2, R5.Pin_1
  N12: Componente1.D2, S1.Pin_1, S1.Pin_2, R3.Pin_1
  N13: U1.E, R6.Pin_0
  N14: U1.G1, R9.Pin_0
  N15: U1.DP, R10.Pin_0
  N16: U1.A, R7.Pin_0
  N17: U1.G2, R12.Pin_0
  N18: U1.G, R11.Pin_0
  N19: S2.Pin_1, S2.Pin_2, R4.Pin_1
  N20: U2.Q1, R6.Pin_1
  N21: U2.Q2, R7.Pin_1
  N22: U2.Q3, R8.Pin_1
  N23: U2.Q4, R9.Pin_1
  N24: U2.Q5, R10.Pin_1
  N25: U2.Q6, R11.Pin_1
  N26: U2.Q7, R12.Pin_1
